// Logisim project computer.circ as structural Verilog: 7 circuits, main circuit main
module main (
  input  IRQ,
  input  in_2,
  input  in_3,
  input  in_4,
  input  in_5,
  input  [3:0] in_6,
  input  [2:0] in_7,
  input  [3:0] in_8,
  input  in_9,
  input  in_10,
  input  in_11,
  input  in_12,
  input  in_13,
  input  in_14,
  input  in_15,
  input  in_16,
  input  in_17,
  input  in_18,
  input  in_19,
  input  in_20,
  input  in_21,
  input  in_22,
  input  [1:0] in_23,
  input  [1:0] in_24,
  input  in_25,
  input  [2:0] in_26,
  input  in_27,
  input  MANUAL_INPUT
);

  wire ADD, AI, AN, and_1_out, and_2_out, and_3_out, and_4_out, and_5_out, and_6_out, and_7_out, and_8_out,
       AO, BIT, BR, CARRY, CF, CLC, CLK, clock_1_out, CLV, CTR, d_ff_1_q, decoder_1_out1, decoder_1_out2,
       decoder_1_out3, decoder_1_out4, decoder_1_out5, decoder_1_out6, decoder_1_out7, DRF, DSP, EI, ETR,
       HLT, IC, IE, multiplexer_1_out, multiplexer_2_out, multiplexer_6_out, multiplexer_10_out, NF, NOP,
       nor_1_out, nor_2_out, nor_3_out, nor_4_out, nor_5_out, nor_6_out, nor_8_out, not_1_out, not_2_out,
       not_3_out, not_4_out, not_5_out, not_6_out, not_7_out, not_8_out, not_9_out, not_10_out, not_11_out,
       not_12_out, not_13_out, OI, or_1_out, or_2_out, or_3_out, or_4_out, or_5_out, or_6_out, or_7_out,
       or_8_out, PCI_DH, PCI_DL, PCO_DH, PCO_DL, pull_resistor_3_node, RI, RO, SC, SEL_CLK, SI, SPAO, SPDO,
       SPI, SRDI, SRDO, START_INSTR, SU, TRHI, VF, XI, XO, XO_X1, XO_X2, YI, YO, YO_X1, YO_X2, ZF;
  wire [1:0] bitselector_2_out;
  wire [2:0] STEP;
  wire [3:0] bitselector_3_out, multiplexer_3_out;
  wire [6:0] bitselector_5_out, Flags;
  wire [7:0] adder_1_out, alu_1_outpt, Aux_Bus1, Aux_Bus2, Aux_Bus3, bitselector_6_out, bitselector_7_out,
       counter_2_q, Data_Bus, demultiplexer_2_out0, demultiplexer_2_out1, IR_OUT, multiplexer_5_out,
       multiplexer_7_out, multiplexer_9_out, multiplexer_11_out, multiplexer_12_out, multiplexer_13_out,
       multiplexer_14_out, multiplexer_15_out, ram_1_data, register_2_q, register_3_q, register_4_q,
       register_5_q, register_6_q, register_7_q, register_8_q, register_9_q, register_10_q, register_11_q,
       register_12_q, register_13_q, rom_1_data, status_register_1_outpt;
  wire [8:0] bit_extender_2_out;
  wire [10:0] ARTH;
  wire [13:0] bitselector_1_out, demultiplexer_1_out0, demultiplexer_1_out1;
  wire [15:0] Address_Bus, Address_Reg, bit_extender_1_out, bit_extender_3_out, multiplexer_4_out,
       multiplexer_16_out, program_counter_1_oupt;
  wire [35:0] CONTROL, rom_2_data;

  not not_1 (not_1_out, Flags[5]);
  and and_1 (and_1_out, IE, CLK);
  and and_2 (and_2_out, IRQ, not_1_out);
  or or_1 (or_1_out, in_3, and_1_out);
  nor nor_1 (nor_1_out, or_1_out, nor_2_out);
  nor nor_2 (nor_2_out, nor_1_out, and_2_out);
  and and_3 (and_3_out, nor_1_out, START_INSTR);
  nor nor_3 (nor_3_out, in_2, nor_4_out);
  nor nor_4 (nor_4_out, nor_3_out, in_3);
  not not_2 (not_2_out, RI);
  BitSelector #(.group(14), .width(16)) bitselector_1 (.in(Address_Reg), .out(bitselector_1_out), .sel(1'b0));
  BitSelector #(.group(2), .width(16)) bitselector_2 (.in(Address_Reg), .out(bitselector_2_out), .sel(3'b111));
  nor nor_5 (nor_5_out, or_1_out, nor_6_out);
  nor nor_6 (nor_6_out, nor_5_out, and_3_out);
  BitSelector #(.group(4)) bitselector_3 (.in(Data_Bus), .out(bitselector_3_out), .sel(1'b0));
  D_Flip_Flop d_ff_1 (.D(CONTROL[17]), .clk(CLK), .Q(d_ff_1_q), .reset(in_3));  // open: Qn, preset
  Multiplexer multiplexer_1 (.in0(CLK), .in1(not_3_out), .out(multiplexer_1_out), .sel(BR));
  not not_3 (not_3_out, CLK);
  Multiplexer multiplexer_2 (.in0(1'b1), .in1(not_2_out), .out(multiplexer_2_out), .sel(RI));
  Demultiplexer #(.width(14)) demultiplexer_1 (
    .out0(demultiplexer_1_out0), .out1(demultiplexer_1_out1), .in(bitselector_1_out), .sel(or_2_out));
  or or_2 (or_2_out, bitselector_2_out[0], bitselector_2_out[1]);
  Multiplexer #(.width(4)) multiplexer_3 (
    .in0({ZF, NF, VF, CF}), .in1(bitselector_3_out), .out(multiplexer_3_out), .sel(SRDI));
  not not_4 (not_4_out, CONTROL[17]);
  and and_4 (and_4_out, CLK, nor_3_out);
  Multiplexer #(.width(16)) multiplexer_4 (.in0(Address_Bus), .in1(16'h4000), .out(multiplexer_4_out), .sel(in_3));
  RAM #(.addrWidth(14), .asyncread("true"), .databus("bidir"), .trigger("falling"), .\type ("nonvolatile")) ram_1 (
    .addr(demultiplexer_1_out0), .we(RI), .oe(multiplexer_2_out), .clk(CLK), .data(ram_1_data));
  ROM #(.addrWidth(16), .misaligned("true")) rom_1 (.addr(bit_extender_1_out), .data(rom_1_data));
  assign bit_extender_1_out = {{2{1'b0}}, demultiplexer_1_out1};  // Bit_Extender bit_extender_1
  and and_5 (and_5_out, CONTROL[16], not_5_out);
  not not_5 (not_5_out, nor_5_out);
  and and_6 (and_6_out, not_4_out, d_ff_1_q);
  Pull_Resistor pull_resistor_1 (.node(STEP));
  Register #(.width(16)) register_1 (
    .D(multiplexer_4_out), .en(or_3_out), .clk(multiplexer_1_out), .Q(Address_Reg), .clr(pull_resistor_3_node));
  or or_3 (or_3_out, CONTROL[35], in_3);
  Pull_Resistor pull_resistor_2 (.node(or_3_out));
  Demultiplexer #(.width(8)) demultiplexer_2 (
    .out0(demultiplexer_2_out0), .out1(demultiplexer_2_out1), .in(multiplexer_5_out), .sel(nor_5_out));
  Multiplexer #(.width(8)) multiplexer_5 (
    .in0(register_2_q), .in1(multiplexer_9_out), .out(multiplexer_5_out), .sel(DRF));
  or or_4 (or_4_out, not_6_out, in_3);
  not not_6 (not_6_out, nor_5_out);
  Multiplexer multiplexer_6 (.in0(and_6_out), .in1(in_3), .out(multiplexer_6_out), .sel(in_3));
  ROM #(.addrWidth(18), .dataWidth(36)) rom_2 (.addr({Flags, IR_OUT, STEP}), .data(rom_2_data));
  Pull_Resistor pull_resistor_3 (.node(pull_resistor_3_node));
  Register #(.trigger("falling")) register_2 (
    .D(multiplexer_9_out), .en(CONTROL[15]), .clk(CLK), .Q(register_2_q), .clr(in_3));
  Register #(.trigger("falling")) register_3 (
    .D(demultiplexer_2_out0), .en(and_5_out), .clk(multiplexer_10_out), .Q(register_3_q), .clr(in_3));
  Register #(.trigger("falling")) register_4 (
    .D(multiplexer_7_out), .en(or_5_out), .clk(multiplexer_10_out), .Q(register_4_q));  // open: clr
  Multiplexer #(.width(8)) multiplexer_7 (
    .in0(demultiplexer_2_out1), .in1(8'h26), .out(multiplexer_7_out), .sel(or_4_out));
  or or_5 (or_5_out, CONTROL[16], IE, in_3);
  Counter #(.max('h7), .trigger("falling"), .width(3)) counter_1 (
    .clr(multiplexer_6_out), .load(1'b0), .up(1'b1), .clk(and_4_out), .Q(STEP));  // open: count, D, carry
  assign ram_1_data = RI ? Data_Bus : 8'bz;  // Controlled_Buffer controlled_buffer_1
  LedBar ledbar_1 (
    .led0(IR_OUT[7]), .led1(IR_OUT[6]), .led2(IR_OUT[5]), .led3(IR_OUT[4]), .led4(IR_OUT[3]),
    .led5(IR_OUT[2]), .led6(IR_OUT[1]), .led7(IR_OUT[0]));
  Multiplexer #(.width(8)) multiplexer_8 (.in0(register_3_q), .in1(register_4_q), .out(IR_OUT), .sel(nor_5_out));
  status_register status_register_1 (
    .CF(multiplexer_3_out[0]), .CLK(SEL_CLK), .FI(CONTROL[18]), .VF(multiplexer_3_out[1]), .RESET(in_3),
    .CLC(CLC), .NF(multiplexer_3_out[2]), .ZF(multiplexer_3_out[3]), .SC(SC), .IC(IC), .SI(SI), .CLV(CLV),
    .ARTH({ARTH[10], AN, ARTH[8:0]}), .BIT(BIT), .outpt(status_register_1_outpt));  // open: CB, CIMG, SB, SIMG
  LedBar ledbar_2 (
    .led0(START_INSTR), .led1(decoder_1_out1), .led2(decoder_1_out2), .led3(decoder_1_out3),
    .led4(decoder_1_out4), .led5(decoder_1_out5), .led6(decoder_1_out6), .led7(decoder_1_out7));
  Decoder #(.select(3)) decoder_1 (
    .out0(START_INSTR), .out1(decoder_1_out1), .out2(decoder_1_out2), .out3(decoder_1_out3),
    .out4(decoder_1_out4), .out5(decoder_1_out5), .out6(decoder_1_out6), .out7(decoder_1_out7), .sel(STEP));  // open: en
  assign Data_Bus = RO ? multiplexer_9_out : 8'bz;  // Controlled_Buffer controlled_buffer_2
  Multiplexer #(.width(8)) multiplexer_9 (.in0(ram_1_data), .in1(rom_1_data), .out(multiplexer_9_out), .sel(or_2_out));
  Multiplexer multiplexer_10 (.in0(CLK), .in1(not_8_out), .out(multiplexer_10_out), .sel(NOP));
  LedBar #(.matrixcols(7)) ledbar_3 (
    .led0(Flags[6]), .led1(Flags[5]), .led2(Flags[4]), .led3(Flags[3]), .led4(Flags[2]), .led5(Flags[1]),
    .led6(Flags[0]));
  BitSelector #(.group(7)) bitselector_4 (.in(status_register_1_outpt), .out(Flags), .sel(1'b0));
  assign Data_Bus = SRDO ? status_register_1_outpt : 8'bz;  // Controlled_Buffer controlled_buffer_3
  assign CONTROL = not_7_out ? rom_2_data : 36'bz;  // Controlled_Buffer controlled_buffer_4
  not not_7 (not_7_out, MANUAL_INPUT);
  not not_8 (not_8_out, CLK);
  Register #(.trigger("falling")) register_5 (.D(Data_Bus), .en(PCI_DH), .clk(CLK), .Q(register_5_q), .clr(in_3));
  or or_6 (or_6_out, SU, ARTH[3]);
  Multiplexer #(.width(8)) multiplexer_11 (.in0(Data_Bus), .in1(Aux_Bus3), .out(multiplexer_11_out), .sel(ETR));
  Multiplexer #(.width(8)) multiplexer_12 (.in0(Data_Bus), .in1(adder_1_out), .out(multiplexer_12_out), .sel(CTR));
  Adder adder_1 (.a(Data_Bus), .b({8{1'b0}}), .out(adder_1_out), .cin(CARRY));  // open: cout
  Register register_6 (.D(Data_Bus), .en(AI), .clk(CLK), .Q(register_6_q), .clr(in_3));
  Multiplexer #(.width(8)) multiplexer_13 (.in0(Aux_Bus2), .in1(Data_Bus), .out(multiplexer_13_out), .sel(CONTROL[9]));
  BitSelector #(.group(7)) bitselector_5 (.in(Data_Bus), .out(bitselector_5_out), .sel(1'b0));
  Register #(.trigger("falling")) register_7 (.D(Data_Bus), .en(PCI_DL), .clk(CLK), .Q(register_7_q), .clr(in_3));
  Multiplexer #(.width(8)) multiplexer_14 (.in0({8{1'b0}}), .in1(Data_Bus), .out(multiplexer_14_out), .sel(SPI));
  Register register_8 (.D(multiplexer_11_out), .en(CONTROL[4]), .clk(CLK), .Q(register_8_q), .clr(in_3));
  Register register_9 (.D(multiplexer_12_out), .en(TRHI), .clk(CLK), .Q(register_9_q), .clr(or_7_out));
  or or_7 (or_7_out, in_3, CONTROL[14]);
  assign Data_Bus = AO ? register_6_q : 8'bz;  // Controlled_Buffer controlled_buffer_5
  Multiplexer #(.width(8)) multiplexer_15 (
    .in0(register_6_q), .in1(Aux_Bus1), .out(multiplexer_15_out), .sel(CONTROL[12]));
  Register register_10 (.D(Data_Bus), .en(XI), .clk(CLK), .Q(register_10_q), .clr(in_3));
  Register register_11 (.D(Data_Bus), .en(YI), .clk(CLK), .Q(register_11_q), .clr(in_3));
  TTY tty_1 (.data(bitselector_5_out), .clk(CLK), .we(OI), .clr(in_3));
  Multiplexer #(.width(16)) multiplexer_16 (
    .in0({register_5_q, register_7_q}), .in1(16'hfffa), .out(multiplexer_16_out), .sel(CONTROL[19]));
  not not_9 (not_9_out, DSP);
  Register #(.trigger("falling")) register_12 (.D(counter_2_q), .en(1'b1), .clk(CLK), .Q(register_12_q), .clr(in_3));
  Counter counter_2 (
    .load(SPI), .D(multiplexer_14_out), .count(CONTROL[20]), .Q(counter_2_q), .up(not_9_out), .clk(CLK),
    .clr(in_3));  // open: carry
  assign Data_Bus = XO ? register_10_q : 8'bz;  // Controlled_Buffer controlled_buffer_6
  assign Aux_Bus1 = XO_X1 ? register_10_q : 8'bz;  // Controlled_Buffer controlled_buffer_7
  assign Aux_Bus2 = XO_X2 ? register_10_q : 8'bz;  // Controlled_Buffer controlled_buffer_8
  assign Data_Bus = YO ? register_11_q : 8'bz;  // Controlled_Buffer controlled_buffer_9
  assign Aux_Bus1 = YO_X1 ? register_11_q : 8'bz;  // Controlled_Buffer controlled_buffer_10
  assign Aux_Bus2 = YO_X2 ? register_11_q : 8'bz;  // Controlled_Buffer controlled_buffer_11
  not not_10 (not_10_out, CTR);
  ALU alu_1 (
    .A(multiplexer_15_out), .B(multiplexer_13_out), .ADD(ADD), .AND_MODE(AN), .OR_MODE(ARTH[8]),
    .XOR_MODE(ARTH[7]), .LSHF_R(ARTH[6]), .ASHF_L(ARTH[5]), .ROT_R(ARTH[4]), .ROT_L(ARTH[0]), .SUB(or_6_out),
    .INC(ARTH[2]), .DEC(ARTH[1]), .FLAGS(Flags), .BIT(BIT), .ECLK(SEL_CLK), .LD(ARTH[10]),
    .outpt(alu_1_outpt), .CF(CF), .NF(NF), .VF(VF), .ZF(ZF));  // open: NOT_MODE
  assign bit_extender_2_out = {{1{1'b1}}, register_12_q};  // Bit_Extender bit_extender_2
  assign Data_Bus = SPDO ? register_12_q : 8'bz;  // Controlled_Buffer controlled_buffer_12
  assign Address_Bus = CONTROL[11] ? {register_9_q, register_8_q} : 16'bz;  // Controlled_Buffer controlled_buffer_13
  or or_8 (or_8_out, in_3, not_10_out);
  and and_7 (and_7_out, CTR, CF);
  assign CONTROL[35] = MANUAL_INPUT ? in_4 : 1'bz;  // Controlled_Buffer controlled_buffer_14
  LedBar #(.matrixcols(16)) ledbar_4 (
    .led0(program_counter_1_oupt[15]), .led1(program_counter_1_oupt[14]), .led2(program_counter_1_oupt[13]),
    .led3(program_counter_1_oupt[12]), .led4(program_counter_1_oupt[11]), .led5(program_counter_1_oupt[10]),
    .led6(program_counter_1_oupt[9]), .led7(program_counter_1_oupt[8]), .led8(program_counter_1_oupt[7]),
    .led9(program_counter_1_oupt[6]), .led10(program_counter_1_oupt[5]), .led11(program_counter_1_oupt[4]),
    .led12(program_counter_1_oupt[3]), .led13(program_counter_1_oupt[2]), .led14(program_counter_1_oupt[1]),
    .led15(program_counter_1_oupt[0]));
  assign bit_extender_3_out = {{7{1'b0}}, bit_extender_2_out};  // Bit_Extender bit_extender_3
  assign Address_Bus = SPAO ? bit_extender_3_out : 16'bz;  // Controlled_Buffer controlled_buffer_15
  Pull_Resistor pull_resistor_4 (.node(Address_Bus));
  Pull_Resistor pull_resistor_5 (.node(Data_Bus));
  Pull_Resistor pull_resistor_6 (.node(Aux_Bus1));
  Pull_Resistor pull_resistor_7 (.node(Aux_Bus2));
  nor nor_7 (CARRY, or_8_out, nor_8_out);
  nor nor_8 (nor_8_out, CARRY, and_7_out);
  Register register_13 (.D(alu_1_outpt), .en(EI), .clk(SEL_CLK), .Q(register_13_q), .clr(in_3));
  assign CONTROL[34] = MANUAL_INPUT ? in_5 : 1'bz;  // Controlled_Buffer controlled_buffer_16
  program_counter program_counter_1 (
    .Load(CONTROL[21]), .Inpt(multiplexer_16_out), .CE(CONTROL[22]), .CLK(CLK), .Reset(in_3),
    .INTERUPT(CONTROL[0]), .Oupt(program_counter_1_oupt));
  Multiplexer multiplexer_17 (.in0(CLK), .in1(not_11_out), .out(SEL_CLK), .sel(CONTROL[10]));
  not not_11 (not_11_out, CLK);
  Decoder #(.enable("false"), .select(4)) decoder_2 (
    .out1(PCI_DL), .out2(PCI_DH), .out3(RI), .out4(EI), .out5(AI), .out6(XI), .out7(YI), .out8(SRDI),
    .out9(SPI), .out10(IC), .out11(TRHI), .out12(OI), .out13(BR), .out14(BIT), .out15(SC),
    .sel(CONTROL[33:30]));  // open: out0
  Decoder #(.enable("false"), .select(4)) decoder_3 (
    .out1(AN), .out2(ARTH[8]), .out3(ARTH[7]), .out4(SU), .out5(ARTH[6]), .out6(ARTH[5]), .out7(ARTH[4]),
    .out8(ARTH[0]), .out9(ARTH[3]), .out10(DSP), .out11(NOP), .out12(SI), .out13(ARTH[2]), .out14(ARTH[1]),
    .out15(ADD), .sel(CONTROL[26:23]));  // open: out0
  assign CONTROL[33:30] = MANUAL_INPUT ? in_6 : 4'bz;  // Controlled_Buffer controlled_buffer_17
  assign CONTROL[29:27] = MANUAL_INPUT ? in_7 : 3'bz;  // Controlled_Buffer controlled_buffer_18
  assign Address_Bus = CONTROL[34] ? program_counter_1_oupt : 16'bz;  // Controlled_Buffer controlled_buffer_19
  assign Data_Bus = PCO_DL ? bitselector_6_out : 8'bz;  // Controlled_Buffer controlled_buffer_20
  BitSelector #(.group(8), .width(16)) bitselector_6 (.in(program_counter_1_oupt), .out(bitselector_6_out), .sel(1'b0));
  assign Data_Bus = PCO_DH ? bitselector_7_out : 8'bz;  // Controlled_Buffer controlled_buffer_21
  BitSelector #(.group(8), .width(16)) bitselector_7 (.in(program_counter_1_oupt), .out(bitselector_7_out), .sel(1'b1));
  not not_12 (not_12_out, CONTROL[4]);
  and and_8 (and_8_out, CONTROL[13], not_12_out);
  assign Data_Bus = and_8_out ? register_13_q : 8'bz;  // Controlled_Buffer controlled_buffer_22
  assign Aux_Bus3 = ETR ? register_13_q : 8'bz;  // Controlled_Buffer controlled_buffer_23
  and and_9 (ETR, CONTROL[13], CONTROL[4]);
  assign CONTROL[26:23] = MANUAL_INPUT ? in_8 : 4'bz;  // Controlled_Buffer controlled_buffer_24
  assign CONTROL[22] = MANUAL_INPUT ? in_9 : 1'bz;  // Controlled_Buffer controlled_buffer_25
  assign CONTROL[21] = MANUAL_INPUT ? in_10 : 1'bz;  // Controlled_Buffer controlled_buffer_26
  assign CONTROL[20] = MANUAL_INPUT ? in_11 : 1'bz;  // Controlled_Buffer controlled_buffer_27
  assign CONTROL[19] = MANUAL_INPUT ? in_12 : 1'bz;  // Controlled_Buffer controlled_buffer_28
  assign CONTROL[18] = MANUAL_INPUT ? in_13 : 1'bz;  // Controlled_Buffer controlled_buffer_29
  assign CONTROL[17] = MANUAL_INPUT ? in_14 : 1'bz;  // Controlled_Buffer controlled_buffer_30
  assign CONTROL[16] = MANUAL_INPUT ? in_15 : 1'bz;  // Controlled_Buffer controlled_buffer_31
  assign CONTROL[15] = MANUAL_INPUT ? in_16 : 1'bz;  // Controlled_Buffer controlled_buffer_32
  assign CONTROL[14] = MANUAL_INPUT ? in_17 : 1'bz;  // Controlled_Buffer controlled_buffer_33
  assign CONTROL[13] = MANUAL_INPUT ? in_18 : 1'bz;  // Controlled_Buffer controlled_buffer_34
  Decoder #(.enable("false"), .select(3)) decoder_4 (
    .out1(PCO_DL), .out2(PCO_DH), .out3(AO), .out4(DRF), .out5(SPDO), .out6(SRDO), .out7(RO),
    .sel(CONTROL[29:27]));  // open: out0
  assign CONTROL[12] = MANUAL_INPUT ? in_19 : 1'bz;  // Controlled_Buffer controlled_buffer_35
  assign CONTROL[11] = MANUAL_INPUT ? in_20 : 1'bz;  // Controlled_Buffer controlled_buffer_36
  assign CONTROL[10] = MANUAL_INPUT ? in_21 : 1'bz;  // Controlled_Buffer controlled_buffer_37
  assign CONTROL[9] = MANUAL_INPUT ? in_22 : 1'bz;  // Controlled_Buffer controlled_buffer_38
  assign CONTROL[8:7] = MANUAL_INPUT ? in_23 : 2'bz;  // Controlled_Buffer controlled_buffer_39
  assign CONTROL[6:5] = MANUAL_INPUT ? in_24 : 2'bz;  // Controlled_Buffer controlled_buffer_40
  Decoder #(.enable("false"), .select(2)) decoder_5 (
    .out1(XO), .out2(XO_X1), .out3(XO_X2), .sel(CONTROL[8:7]));  // open: out0
  assign CONTROL[4] = MANUAL_INPUT ? in_25 : 1'bz;  // Controlled_Buffer controlled_buffer_41
  assign CONTROL[3:1] = MANUAL_INPUT ? in_26 : 3'bz;  // Controlled_Buffer controlled_buffer_42
  assign CONTROL[0] = MANUAL_INPUT ? in_27 : 1'bz;  // Controlled_Buffer controlled_buffer_43
  Decoder #(.enable("false"), .select(3)) decoder_6 (
    .out1(CTR), .out2(IE), .out3(CLC), .out4(HLT), .out5(CLV), .out6(ARTH[10]), .out7(SPAO),
    .sel(CONTROL[3:1]));  // open: out0
  Decoder #(.enable("false"), .select(2)) decoder_7 (
    .out1(YO), .out2(YO_X1), .out3(YO_X2), .sel(CONTROL[6:5]));  // open: out0
  Clock clock_1 (.out(clock_1_out));
  not not_13 (not_13_out, HLT);
  and and_10 (CLK, clock_1_out, not_13_out);

  // Other names for the same wires on the sheet: ROT_L = ARTH[0]; DEC = ARTH[1]; INC = ARTH[2]; CMP = ARTH[3];
  //   ROT_R = ARTH[4]; ASHF_L = ARTH[5]; LSHF_R = ARTH[6]; EOR = ARTH[7]; ORA = ARTH[8]; ARTH[9] = AN; LD = ARTH[10];
  //   CSB = CONTROL[0]; TRLI = CONTROL[4]; ES2 = CONTROL[9]; ECLK = CONTROL[10]; TRO = CONTROL[11]; ES1 = CONTROL[12];
  //   EO = CONTROL[13]; RTR = CONTROL[14]; FETCH = CONTROL[15]; II = CONTROL[16]; EP = CONTROL[17]; FI = CONTROL[18];
  //   IJ = CONTROL[19]; SPE = CONTROL[20]; J = CONTROL[21]; PCE = CONTROL[22]; D_3[3:0] = CONTROL[26:23];
  //   D_2[2:0] = CONTROL[29:27]; D_1[3:0] = CONTROL[33:30]; PCO_A = CONTROL[34]; MI = CONTROL[35];
  //   D_4[2:0] = CONTROL[3:1]; Interupt_Flag = Flags[5]; Reset = in_3; SHUTDOWN = in_2; XREG[1:0] = CONTROL[8:7];
  //   YREG[1:0] = CONTROL[6:5]

  // Notes on the sheet:
  //   Interupt Handler
  //   contents of rom_1 (hex, n*v repeats v):
  //   5b 3 1 ff a3 1 3d 1 50 1 20 10 40 58 8 40 bb
  //   contents of rom_2 (hex, n*v repeats v):
  //   8000 c00430000 6*0 d38448200 d40432000 6*0 c3840c410 938040e00 d40432000 5*0 d3fc09300 6410
  //   938040e00 d40432000 4*0 d3fc09240 6410 938040e00 d40432000 4*0 c38400010 ef8408400 938040e00
  //   d40432000 4*0 d3fc01302 ef840a412 938040e00 d40432000 4*0 d3fc01242 ef840a412 938040e00 d40432000
  //   4*0 d3fc09300 6010 800000800 38000410 938040e00 d40432000 0 0 d3fc09240 6010 800000800 38000410
  //   938040e00 d40432000 0 0 c3840c410 93f801f02 2c0002412 938040e00 d40432000 0 0 0 c3840c410 93f801e42
  //   2c0002412 938040e00 d40432000 0 0 0 d38c08200 d40432000 6*0 c3840c410 938800e00 d40432000 5*0
  //   d3fc09300 6410 938800e00 d40432000 4*0 d3fc09240 6410 938800e00 d40432000 4*0 c38400010 ef8408400
  //   938800e00 d40432000 4*0 d3fc01302 ef840a412 938800e00 d40432000 4*0 d3fc01242 ef840a412 938800e00
  //   d40432000 4*0 d3fc09300 6010 800000800 38000410 938800e00 d40432000 0 0 d3fc09240 6010 800000800
  //   38000410 938800e00 d40432000 0 0 c3840c410 93f801f02 2c0002412 938800e00 d40432000 0 0 0 c3840c410
  //   93f801e42 2c0002412 938800e00 d40432000 0 0 0 d03408000 d40432000 6*0 c3840c010 800000800 178000000
  //   103000000 d40432000 0 0 0 d3fc09300 6010 800000800 178000000 103000000 d40432000 0 0 d3fc09240 6010
  //   800000800 178000000 103000000 d40432000 0 0 c38400010 ef8408000 800000800 178000000 103000000
  //   d40432000 0 0 d3fc01302 ef840a412 800000800 178000000 103000000 d40432000 0 0 d3fc01242 ef840a412
  //   800000800 178000000 103000000 d40432000 0 0 78000000 cb8000000 f40200000 f40408000 430000 0 0 0
  //   c00400000 c00408000 c00400000 30000 4*0 c00400000 c00408000 c00400000 30000 4*0 c3840c410 bb8000e00
  //   c00430000 5*0 c38400010 ef8408400 bb8000e00 c00430000 4*0 c00400000 c00408000 c00400000 30000 4*0
  //   78000000 cb8000000 f40200000 f40408000 430000 0 0 0 78000000 cb8000000 f40200000 f40408000 430000 0
  //   0 0 8d610000f 8c810000f 8f010000e f40280000 f40408000 430000 0 0 78000000 cb8000000 f40200000
  //   f40408000 430000 0 0 0 c00400000 c00408000 c00400000 30000 4*0 8006 c00430000 6*0 280008000
  //   c00430000 6*0 800a c00430000 6*0 c3cc08200 c00430000 6*0 c3840c410 83c800e00 c00430000 5*0 d3fc09300
  //   6410 83c800e00 c00430000 4*0 d3fc09240 6410 83c800e00 c00430000 4*0 c38400010 ef8408400 83c800e00
  //   c00430000 4*0 d3fc01302 ef840a412 83c800e00 c00430000 4*0 d3fc01242 ef840a412 83c800e00 c00430000
  //   4*0 d3fc09300 6010 800000800 38000410 83c800e00 c00430000 0 0 d3fc09240 6010 800000800 38000410
  //   83c800e00 c00430000 0 0 c3840c410 93f801f02 2c0002412 83c800e00 c00430000 0 0 0 c3840c410 93f801e42
  //   2c0002412 83c800e00 c00430000 0 0 0 c3cc09300 c00430000 6*0 c3840c410 83c801f00 c00430000 5*0
  //   c38400010 ef8408400 83c801f00 c00430000 4*0 c3cc09240 c00430000 6*0 c3840c410 83c801e40 c00430000
  //   5*0 c38400010 ef8408400 83c801e40 c00430000 4*0 c3840c410 93f000e00 c0002000 c00430000 4*0 d3fc09300
  //   6410 93f000e00 c0002000 c00430000 0 0 0 d3fc09240 6410 93f000e00 c0002000 c00430000 0 0 0 c38400010
  //   ef8408400 93f000e00 c0002000 c00430000 0 0 0 d3fc01302 ef840a412 93f000e00 c0002000 c00430000 0 0 0
  //   d3fc01242 ef840a412 93f000e00 c0002000 c00430000 0 0 0 d07408380 d80432000 6*0 d07408260 dc0432000
  //   6*0 d39c08200 d40432000 6*0 c3840c410 939800e00 d40432000 5*0 d3fc09300 6410 939800e00 d40432000 4*0
  //   d3fc09240 6410 939800e00 d40432000 4*0 c38400010 ef8408400 939800e00 d40432000 4*0 d3fc01302
  //   ef840a412 939800e00 d40432000 4*0 d3fc01242 ef840a412 939800e00 d40432000 4*0 d3fc09300 6010
  //   800000800 38000410 939800e00 d40432000 0 0 d3fc09240 6010 800000800 38000410 939800e00 d40432000 0 0
  //   c3840c410 93f801f02 2c0002412 939800e00 d40432000 0 0 0 c3840c410 93f801e42 2c0002412 939800e00
  //   d40432000 0 0 0 c3840c410 93e800e00 c0002000 c00430000 4*0 d3fc09300 6410 93e800e00 c0002000
  //   c00430000 0 0 0 d3fc09240 6410 93e800e00 c0002000 c00430000 0 0 0 c38400010 ef8408400 93e800e00
  //   c0002000 c00430000 0 0 0 d3fc01302 ef840a412 93e800e00 c0002000 c00430000 0 0 0 d3fc01242 ef840a412
  //   93e800e00 c0002000 c00430000 0 0 0 d06c08380 d80432000 6*0 d07408260 dc0432000 6*0 78000000
  //   cb8000000 f40200000 f40408000 430000 0 0 0 78000000 cb8000000 f40200000 78400000 cb8000000 f40408000
  //   430000 0 780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
  //   Memory Address Register
  //   Status Register
  //   Sequencer
  //   Instruction Register
  //   Accumulator
  //   IRQ
  //   Transfer Register
  //   Register X
  //   Register Y
  //   Output Terminal
  //   Stack Pointer
  //   Program Counter
  //   Control Ward
endmodule

module program_counter (
  input  Load,
  input  [15:0] Inpt,
  input  CE,
  input  CLK,
  input  Reset,
  input  INTERUPT,
  output [15:0] Oupt
);

  wire and_1_out, not_1_out, or_1_out;
  wire [15:0] counter_1_q, multiplexer_1_out, subtractor_1_out;

  Multiplexer #(.width(16)) multiplexer_1 (.in0(Inpt), .in1(16'h4001), .out(multiplexer_1_out), .sel(Reset));
  or or_1 (or_1_out, Load, Reset);
  Counter #(.max('hffff), .width(16)) counter_1 (
    .load(or_1_out), .D(multiplexer_1_out), .count(CE), .Q(counter_1_q), .up(1'b1), .clk(CLK));  // open: carry, clr
  Subtractor #(.width(16)) subtractor_1 (.a(counter_1_q), .b(16'h1), .out(subtractor_1_out));  // open: bin, bout
  Multiplexer #(.width(16)) multiplexer_2 (.in0(counter_1_q), .in1(subtractor_1_out), .out(Oupt), .sel(and_1_out));
  and and_1 (and_1_out, INTERUPT, not_1_out);
  not not_1 (not_1_out, Load);

  // Other names for the same wires on the sheet: J = Load
endmodule

module ALU (
  input  [7:0] A,
  input  [7:0] B,
  input  ADD,
  input  AND_MODE,
  input  OR_MODE,
  input  XOR_MODE,
  input  NOT_MODE,
  input  LSHF_R,
  input  ASHF_L,
  input  ROT_R,
  input  ROT_L,
  input  SUB,
  input  INC,
  input  DEC,
  input  [6:0] FLAGS,
  input  BIT,
  input  ECLK,
  input  LD,
  output [7:0] outpt,
  output CF,
  output NF,
  output VF,
  output ZF
);

  wire adder_1_cout, bitselector_1_out, bitselector_2_out, multiplexer_1_out, or_2_out, or_3_out, OUTPUT_SEL,
       overflow_checker_1_vf, subtractor_1_bout;
  wire [7:0] adder_1_out, adder_2_out, and_1_out, multiplexer_2_out, not_1_out, or_1_out, subtractor_1_out,
       subtractor_2_out, xor_1_out;

  assign and_1_out = A & B;  // AND_Gate and_1, 8 bits wide
  assign or_1_out = A | B;  // OR_Gate or_1, 8 bits wide
  assign xor_1_out = A ^ B;  // XOR_Gate xor_1, 8 bits wide
  assign not_1_out = ~A;  // NOT_Gate not_1, 8 bits wide
  or or_2 (or_2_out, AND_MODE, BIT);
  assign outpt = or_2_out ? and_1_out : 8'bz;  // Controlled_Buffer controlled_buffer_1
  assign outpt = OR_MODE ? or_1_out : 8'bz;  // Controlled_Buffer controlled_buffer_2
  assign outpt = XOR_MODE ? xor_1_out : 8'bz;  // Controlled_Buffer controlled_buffer_3
  assign outpt = NOT_MODE ? not_1_out : 8'bz;  // Controlled_Buffer controlled_buffer_4
  BitSelector #(.width(7)) bitselector_1 (.in(FLAGS), .out(bitselector_1_out), .sel(3'b000));
  Multiplexer multiplexer_1 (.in0(bitselector_1_out), .in1(1'b0), .out(multiplexer_1_out), .sel(or_3_out));
  or or_3 (or_3_out, ADD, LD);
  Adder adder_1 (.a(A), .b(B), .out(adder_1_out), .cin(multiplexer_1_out), .cout(adder_1_cout));
  Subtractor subtractor_1 (.a(A), .b(B), .out(subtractor_1_out), .bin(multiplexer_1_out), .bout(subtractor_1_bout));
  overflow_checker overflow_checker_1 (.A(A), .B(B), .O(outpt), .S(SUB), .VF(overflow_checker_1_vf));
  Multiplexer #(.width(8)) multiplexer_2 (
    .in0(adder_1_out), .in1(subtractor_1_out), .out(multiplexer_2_out), .sel(SUB));
  Multiplexer multiplexer_3 (.in0(adder_1_cout), .in1(subtractor_1_bout), .out(CF), .sel(SUB));
  Multiplexer multiplexer_4 (.in0(overflow_checker_1_vf), .in1(B[6]), .out(VF), .sel(BIT));
  nor nor_1 (OUTPUT_SEL, BIT, DEC, ROT_L, ASHF_L, AND_MODE, OR_MODE, NOT_MODE, XOR_MODE, LSHF_R, ROT_R, INC);
  assign outpt = OUTPUT_SEL ? multiplexer_2_out : 8'bz;  // Controlled_Buffer controlled_buffer_5
  BitSelector bitselector_2 (.in(outpt), .out(bitselector_2_out), .sel(3'b111));
  Multiplexer multiplexer_5 (.in0(bitselector_2_out), .in1(B[7]), .out(NF), .sel(BIT));
  zero_checker zero_checker_1 (.inpt(outpt), .oupt(ZF));
  Adder adder_2 (.a(B), .b(8'h1), .out(adder_2_out));  // open: cin, cout
  assign outpt = LSHF_R ? {1'b0, A[7:1]} : 8'bz;  // Controlled_Buffer controlled_buffer_6
  assign outpt = ROT_L ? {A[6:0], A[7]} : 8'bz;  // Controlled_Buffer controlled_buffer_7
  assign outpt = INC ? adder_2_out : 8'bz;  // Controlled_Buffer controlled_buffer_8
  assign outpt = DEC ? subtractor_2_out : 8'bz;  // Controlled_Buffer controlled_buffer_9
  Subtractor subtractor_2 (.a(B), .b(8'h1), .out(subtractor_2_out));  // open: bin, bout
  assign outpt = ASHF_L ? {A[6:0], A[7]} : 8'bz;  // Controlled_Buffer controlled_buffer_10
  assign outpt = ROT_R ? {A[0], A[7:1]} : 8'bz;  // Controlled_Buffer controlled_buffer_11

  // Other names for the same wires on the sheet: AND_M = AND_MODE; M6 = B[6]; M7 = B[7]; NOT_M = NOT_MODE;
  //   OR_M = OR_MODE; XOR_M = XOR_MODE

  // Notes on the sheet:
  //   Logical Operators
  //   Overflow Checker
  //   Two's Complement Adder/Subtractor
  //   Zero Checker
endmodule

module zero_checker (
  input  [7:0] inpt,
  output oupt
);

  wire and_1_out, and_2_out, nor_1_out, nor_2_out, nor_3_out, nor_4_out;

  nor nor_1 (nor_1_out, inpt[0], inpt[1]);
  nor nor_2 (nor_2_out, inpt[2], inpt[3]);
  nor nor_3 (nor_3_out, inpt[4], inpt[5]);
  nor nor_4 (nor_4_out, inpt[6], inpt[7]);
  and and_1 (and_1_out, nor_1_out, nor_2_out);
  and and_2 (and_2_out, nor_3_out, nor_4_out);
  and and_3 (oupt, and_1_out, and_2_out);

  // Notes on the sheet:
  //   Zero Checker
endmodule

module status_register (
  input  CF,
  input  CLK,
  input  FI,
  input  CB,
  input  CIMG,
  input  VF,
  input  RESET,
  input  SB,
  input  SIMG,
  input  CLC,
  input  NF,
  input  ZF,
  input  SC,
  input  IC,
  input  SI,
  input  CLV,
  input  [10:0] ARTH,
  input  BIT,
  output [7:0] outpt
);

  wire and_1_out, and_2_out, and_3_out, and_4_out, and_5_out, and_6_out, and_7_out, and_8_out, CI, NI,
       nor_2_out, nor_4_out, nor_6_out, not_1_out, not_2_out, not_3_out, not_4_out, or_1_out, or_2_out,
       or_3_out, or_4_out, or_5_out, or_6_out, or_7_out, or_8_out, or_9_out, or_10_out, or_11_out, or_12_out,
       or_13_out, or_14_out, or_15_out, VI, ZI;

  or or_1 (or_1_out, FI, CI);
  or or_2 (or_2_out, FI, NI);
  and and_1 (and_1_out, CF, or_1_out);
  not not_1 (not_1_out, or_1_out);
  and and_2 (and_2_out, not_1_out, outpt[0]);
  and and_3 (and_3_out, VF, or_3_out);
  or or_3 (or_3_out, FI, VI);
  not not_2 (not_2_out, or_3_out);
  and and_4 (and_4_out, not_2_out, outpt[1]);
  and and_5 (and_5_out, NF, or_2_out);
  not not_3 (not_3_out, or_2_out);
  and and_6 (and_6_out, not_3_out, outpt[2]);
  and and_7 (and_7_out, ZF, or_4_out);
  or or_4 (or_4_out, FI, ZI);
  not not_4 (not_4_out, or_4_out);
  and and_8 (and_8_out, not_4_out, outpt[3]);
  or or_5 (or_5_out, and_1_out, and_2_out);
  or or_6 (or_6_out, and_3_out, and_4_out);
  or or_7 (or_7_out, and_5_out, and_6_out);
  or or_8 (or_8_out, and_7_out, and_8_out);
  or or_9 (or_9_out, RESET, CB);
  or or_10 (or_10_out, RESET, IC);
  or or_11 (or_11_out, RESET, CIMG);
  D_Flip_Flop d_ff_1 (.D(or_5_out), .clk(CLK), .Q(outpt[0]), .preset(SC), .reset(or_12_out));  // open: Qn
  or or_12 (or_12_out, CLC, RESET);
  D_Flip_Flop d_ff_2 (.D(or_6_out), .clk(CLK), .Q(outpt[1]), .reset(or_13_out));  // open: Qn, preset
  or or_13 (or_13_out, CLV, RESET);
  D_Flip_Flop d_ff_3 (.D(or_7_out), .clk(CLK), .Q(outpt[2]), .reset(RESET));  // open: Qn, preset
  D_Flip_Flop d_ff_4 (.D(or_8_out), .clk(CLK), .Q(outpt[3]), .reset(RESET));  // open: Qn, preset
  nor nor_1 (outpt[4], or_9_out, nor_2_out);
  nor nor_2 (nor_2_out, outpt[4], SB);
  nor nor_3 (outpt[5], or_10_out, nor_4_out);
  nor nor_4 (nor_4_out, outpt[5], SI);
  nor nor_5 (outpt[6], or_11_out, nor_6_out);
  nor nor_6 (nor_6_out, outpt[6], SIMG);
  assign NI = BIT ? BIT : 1'bz;  // Controlled_Buffer controlled_buffer_1
  assign ZI = BIT ? BIT : 1'bz;  // Controlled_Buffer controlled_buffer_2
  assign VI = BIT ? BIT : 1'bz;  // Controlled_Buffer controlled_buffer_3
  assign NI = or_14_out ? or_14_out : 1'bz;  // Controlled_Buffer controlled_buffer_4
  assign ZI = or_14_out ? or_14_out : 1'bz;  // Controlled_Buffer controlled_buffer_5
  or or_14 (or_14_out, ARTH[6], ARTH[5], ARTH[3], ARTH[0], ARTH[4]);
  assign CI = or_14_out ? or_14_out : 1'bz;  // Controlled_Buffer controlled_buffer_6
  Pull_Resistor pull_resistor_1 (.node(NI));
  Pull_Resistor pull_resistor_2 (.node(ZI));
  Pull_Resistor pull_resistor_3 (.node(CI));
  Pull_Resistor pull_resistor_4 (.node(VI));
  assign NI = or_15_out ? or_15_out : 1'bz;  // Controlled_Buffer controlled_buffer_7
  assign ZI = or_15_out ? or_15_out : 1'bz;  // Controlled_Buffer controlled_buffer_8
  or or_15 (or_15_out, ARTH[9], ARTH[8], ARTH[7], ARTH[2], ARTH[1], ARTH[10]);

  assign outpt[7] = 1'b0;

  // Other names for the same wires on the sheet: ROT_L = ARTH[0]; DEC = ARTH[1]; INC = ARTH[2]; CMP = ARTH[3];
  //   ROT_R = ARTH[4]; ASHF_L = ARTH[5]; LSHF_R = ARTH[6]; EOR = ARTH[7]; ORA = ARTH[8]; AN = ARTH[9]; LD = ARTH[10]
endmodule

module overflow_checker (
  input  [7:0] A,
  input  [7:0] B,
  input  [7:0] O,
  input  S,
  output VF
);

  wire and_1_out, and_2_out, and_3_out, and_4_out, and_5_out, and_6_out, and_7_out, and_8_out, and_9_out,
       and_10_out, bitselector_1_out, bitselector_2_out, bitselector_3_out, bitselector_4_out,
       bitselector_5_out, bitselector_6_out, nor_1_out, nor_2_out, not_1_out, not_2_out, not_3_out, or_1_out,
       or_2_out, xnor_1_out, xnor_2_out;

  BitSelector bitselector_1 (.in(O), .out(bitselector_1_out), .sel(3'b111));
  BitSelector bitselector_2 (.in(B), .out(bitselector_2_out), .sel(3'b111));
  BitSelector bitselector_3 (.in(A), .out(bitselector_3_out), .sel(3'b111));
  BitSelector bitselector_4 (.in(A), .out(bitselector_4_out), .sel(3'b111));
  BitSelector bitselector_5 (.in(B), .out(bitselector_5_out), .sel(3'b111));
  BitSelector bitselector_6 (.in(O), .out(bitselector_6_out), .sel(3'b111));
  not not_1 (not_1_out, bitselector_1_out);
  and and_1 (and_1_out, not_1_out, and_2_out);
  and and_2 (and_2_out, bitselector_2_out, bitselector_3_out);
  xnor xnor_1 (xnor_1_out, bitselector_2_out, bitselector_3_out);
  nor nor_1 (nor_1_out, bitselector_2_out, bitselector_3_out);
  and and_3 (and_3_out, nor_1_out, bitselector_1_out);
  not not_2 (not_2_out, bitselector_4_out);
  and and_4 (and_4_out, not_2_out, and_5_out);
  and and_5 (and_5_out, bitselector_5_out, bitselector_6_out);
  xnor xnor_2 (xnor_2_out, bitselector_5_out, bitselector_6_out);
  nor nor_2 (nor_2_out, bitselector_5_out, bitselector_6_out);
  and and_6 (and_6_out, nor_2_out, bitselector_4_out);
  and and_7 (and_7_out, and_1_out, xnor_1_out);
  or or_1 (or_1_out, and_8_out, and_6_out);
  and and_8 (and_8_out, and_4_out, xnor_2_out);
  or or_2 (or_2_out, and_7_out, and_3_out);
  and and_9 (and_9_out, or_2_out, not_3_out);
  not not_3 (not_3_out, S);
  and and_10 (and_10_out, S, or_1_out);
  or or_3 (VF, and_9_out, and_10_out);
endmodule

module sequencer (
  input  in_1,
  input  in_2,
  input  in_3,
  input  in_4,
  output out_5,
  output [2:0] out_6
);

  wire and_1_out, and_2_out, decoder_1_out1, decoder_1_out2, decoder_1_out3, decoder_1_out4, decoder_1_out5,
       decoder_1_out6, decoder_1_out7, multiplexer_1_out, nor_1_out, nor_2_out;

  nor nor_1 (nor_1_out, in_4, nor_2_out);
  nor nor_2 (nor_2_out, nor_1_out, in_1);
  and and_1 (and_1_out, in_3, nor_1_out);
  and and_2 (and_2_out, in_2, in_3);
  Multiplexer multiplexer_1 (.in0(and_2_out), .in1(in_1), .out(multiplexer_1_out), .sel(in_1));
  Counter #(.max('h7), .width(3)) counter_1 (
    .clr(multiplexer_1_out), .load(1'b0), .up(1'b1), .clk(and_1_out), .Q(out_6));  // open: count, D, carry
  LedBar ledbar_1 (
    .led0(out_5), .led1(decoder_1_out1), .led2(decoder_1_out2), .led3(decoder_1_out3), .led4(decoder_1_out4),
    .led5(decoder_1_out5), .led6(decoder_1_out6), .led7(decoder_1_out7));
  Decoder #(.select(3)) decoder_1 (
    .out0(out_5), .out1(decoder_1_out1), .out2(decoder_1_out2), .out3(decoder_1_out3), .out4(decoder_1_out4),
    .out5(decoder_1_out5), .out6(decoder_1_out6), .out7(decoder_1_out7), .sel(out_6));  // open: en

  // Other names for the same wires on the sheet: CLK = in_3; END_INSTR = in_2; Reset = in_1; SHUTDOWN = in_4;
  //   START_INSTR = out_5; STEP[2:0] = out_6

  // Notes on the sheet:
  //   Sequencer
endmodule
